# Fritzing sketch not-kiwi-bot (saved by Fritzing 0.9.3b)
circuit board: 14.1997cm x 7.74037cm

parts:
  Raspberry_Pi_1 = Raspberry Pi 3 [part_number=RPI-3-V1.2]
  GP-20U7 = GP-20U7

nets (from the breadboard view):
  3V3: Raspberry_Pi_1.3v3, Raspberry_Pi_1.3V3, GP-20U7.VCC
  N1: Raspberry_Pi_1.GPIO15, GP-20U7.TX
  GND: Raspberry_Pi_1.GND, GP-20U7.GND
